# Fritzing sketch chronodotleddisplay (saved by Fritzing 0.7.5b)
breadboards: 2

parts:
  IC1 = IC, DIP package, 24 pins [chip_label=MAX7217 spacing=300mil part_number=MAX7217CNG]
  LED7Seg = mystery part, 14 pins [chip_label="LED Display" spacing=300mil]
  Arduino1 = Arduino
  Chronodot = mystery part, 8 pins [chip_label=Chronodot spacing=300mil]
  S1 = Pushbutton [package="[THT]"]
  S2 = Pushbutton [package="[THT]"]
  R1 = Resistor [tolerance=±5% resistance=10k package=THT]
  R5 = Resistor [tolerance=±5% resistance=10k package=THT]
  R6 = Resistor [tolerance=±5% resistance=47 package=THT]
  C1 = Electrolytic Capacitor [capacitance=10µF package="100 mil [THT, electrolytic]"]
  C2 = Ceramic Capacitor [capacitance=0.1mF package="100 mil [THT, multilayer]"]
  RSET = Resistor [tolerance=±5% resistance=22k package=THT]

nets:
  N1: IC1.pin1, Arduino1.D11
  N2: IC1.pin2, LED7Seg.pin14
  N3: IC1.pin4, IC1.pin9, Arduino1.GND, Chronodot.pin4, R1.Pin_1, R5.Pin_1, C1.-, C2.0
  N4: IC1.pin6, LED7Seg.pin10
  N5: IC1.pin7, LED7Seg.pin6
  N6: IC1.pin11, LED7Seg.pin11
  N7: IC1.pin12, Arduino1.D10
  N8: IC1.pin13, Arduino1.D13
  N9: IC1.pin14, LED7Seg.pin5
  N10: IC1.pin15, LED7Seg.pin9
  N11: IC1.pin16, LED7Seg.pin12
  N12: IC1.pin17, LED7Seg.pin13
  N13: IC1.pin18, RSET.Pin_0
  N14: IC1.pin19, LED7Seg.pin8, Arduino1.+5V, Chronodot.pin3, S1.Pin_1, S1.Pin_2, S2.Pin_1, S2.Pin_2, C1.+, C2.1, RSET.Pin_1
  N15: IC1.pin20, LED7Seg.pin1
  N16: IC1.pin21, LED7Seg.pin4
  N17: IC1.pin22, LED7Seg.pin3
  N18: IC1.pin23, LED7Seg.pin2
  N19: LED7Seg.pin7, R6.Pin_0
  N20: Arduino1.D9, R6.Pin_1
  N21: Arduino1.D3, S2.Pin_3, S2.Pin_4, R5.Pin_0
  N22: Arduino1.D2, S1.Pin_3, S1.Pin_4, R1.Pin_0
  N23: Arduino1.A4, Chronodot.pin1
  N24: Arduino1.A5, Chronodot.pin2
